// Digital circuit Byter-01.dig as structural Verilog
module Byter_01 (
  input  clk,
  input  IR4,
  input  IR5,
  input  IR6,
  input  STEP_nRUN,
  output Fout,
  output LDA,
  output SETC,
  output RES,
  output RUN,
  output T0,
  output GCLK,
  output RST,
  output CLK_2
);

  wire ADD, AND, Aout, Bout, BUS0, BUS1, BUS2, BUS3, BUS4, BUS5, BUS6, BUS7, button_1_out, button_2_out,
       button_3_out, button_4_out, button_5_out, button_6_out, button_7_out, button_8_out, button_9_out, C,
       Cin, CL0, CL1, CL2, CL3, CLA, CLR, Cout, D0, D1, D2, D3, D4, D5, D6, D7, d_ff_1_nq, d_ff_2_nq,
       d_ff_3_nq, d_ff_4_nq, d_ff_5_nq, d_ff_6_nq, diodeforward_1_out, F, I0, I1, IC16_2_nq, IC16_nq, LOAD,
       nA, nand_2_out, nand_5_out, nand_6_out, nand_7_out, nand_9_out, nand_10_out, nand_11_out, nand_12_out,
       nand_13_out, nand_14_out, nand_15_out, nB, nID0, nID1, nID2, nID3, nID4, nID5, nID6, nJMP, nLDB,
       nZERO, OR, RUN_t, ST, SUB, U5_pin9, U8_pin15, XOR, xor_1_out, xor_2_out, xor_3_out, xor_4_out, Z;
  wire [3:0] U6_pin6;
  wire [3:1] U6_pin10;

  Multiplexer multiplexer_1 (.sel(STEP_nRUN), .in_0(RUN_t), .in_1(button_1_out), .out(RUN));
  Monoflop monoflop_1 (.C(RUN), .R(1'b0), .Q(LDA), .nQ(nLDB));
  Button button_1 (.out(button_1_out));
  Monoflop monoflop_2 (.C(nLDB), .R(1'b0), .Q(SETC), .nQ(RES));
  _74165 U4 (
    .pin1(nLDB), .pin2(GCLK), .pin3(D3), .pin4(D2), .pin5(D1), .pin6(D0), .pin8(1'b0), .pin9(Bout),
    .pin10(1'b0), .pin11(D7), .pin12(D6), .pin13(D5), .pin14(D4), .pin15(1'b0), .pin16(1'b1));  // open: pin7
  LED led_1 (.in(D7));
  D_FF IC16 (.D(IC16_nq), .C(button_2_out), .Q(D7), .nQ(IC16_nq));
  Button button_2 (.out(button_2_out));
  LED led_2 (.in(D6));
  D_FF d_ff_1 (.D(d_ff_1_nq), .C(button_3_out), .Q(D6), .nQ(d_ff_1_nq));
  Button button_3 (.out(button_3_out));
  LED led_3 (.in(D5));
  D_FF d_ff_2 (.D(d_ff_2_nq), .C(button_4_out), .Q(D5), .nQ(d_ff_2_nq));
  Button button_4 (.out(button_4_out));
  LED led_4 (.in(D4));
  D_FF d_ff_3 (.D(d_ff_3_nq), .C(button_5_out), .Q(D4), .nQ(d_ff_3_nq));
  Button button_5 (.out(button_5_out));
  LED led_5 (.in(D3));
  D_FF d_ff_4 (.D(d_ff_4_nq), .C(button_6_out), .Q(D3), .nQ(d_ff_4_nq));
  Button button_6 (.out(button_6_out));
  LED led_6 (.in(D2));
  D_FF d_ff_5 (.D(d_ff_5_nq), .C(button_7_out), .Q(D2), .nQ(d_ff_5_nq));
  Button button_7 (.out(button_7_out));
  LED led_7 (.in(D1));
  D_FF d_ff_6 (.D(d_ff_6_nq), .C(button_8_out), .Q(D1), .nQ(d_ff_6_nq));
  Button button_8 (.out(button_8_out));
  LED led_8 (.in(D0));
  D_FF IC16_2 (.D(IC16_2_nq), .C(button_9_out), .Q(D0), .nQ(IC16_2_nq));
  Button button_9 (.out(button_9_out));
  _74595 U5 (
    .pin1(BUS6), .pin2(BUS5), .pin3(BUS4), .pin4(BUS3), .pin5(BUS2), .pin6(BUS1), .pin7(BUS0), .pin8(1'b0),
    .pin9(U5_pin9), .pin10(RES), .pin11(GCLK), .pin12(T0), .pin13(1'b0), .pin14(Fout), .pin15(BUS7),
    .pin16(1'b1));
  Seven_Seg_Hex seven_seg_hex_1 (.d({D7, D6, D5, D4}), .dp(1'b0));
  Seven_Seg_Hex seven_seg_hex_2 (.d({D3, D2, D1, D0}), .dp(1'b0));
  Seven_Seg_Hex seven_seg_hex_3 (.d({BUS7, BUS6, BUS5, BUS4}), .dp(1'b0));
  DiodeForward diodeforward_1 (.in(BUS7), .out(diodeforward_1_out));
  DiodeForward diodeforward_2 (.in(BUS6), .out(diodeforward_1_out));
  DiodeForward diodeforward_3 (.in(BUS5), .out(diodeforward_1_out));
  DiodeForward diodeforward_4 (.in(BUS4), .out(diodeforward_1_out));
  DiodeForward diodeforward_5 (.in(BUS3), .out(diodeforward_1_out));
  DiodeForward diodeforward_6 (.in(BUS2), .out(diodeforward_1_out));
  DiodeForward diodeforward_7 (.in(BUS1), .out(diodeforward_1_out));
  DiodeForward diodeforward_8 (.in(BUS0), .out(diodeforward_1_out));
  _74138 U1 (
    .pin1(IR4), .pin2(IR5), .pin3(IR6), .pin4(1'b0), .pin5(1'b0), .pin6(1'b1), .pin7(nJMP), .pin8(1'b0),
    .pin9(ST), .pin10(SUB), .pin11(ADD), .pin12(XOR), .pin13(OR), .pin14(AND), .pin15(LOAD), .pin16(1'b1));
  Seven_Seg_Hex seven_seg_hex_4 (.d({BUS3, BUS2, BUS1, BUS0}), .dp(1'b0));
  PullDown pulldown_1 (.out(diodeforward_1_out));
  LED led_9 (.in(diodeforward_1_out));
  nand nand_1 (nZERO, diodeforward_1_out, diodeforward_1_out);
  PullUp pullup_1 (.out(nID6));
  DiodeBackward diodebackward_1 (.in(LOAD), .out(nID6));
  DiodeBackward diodebackward_2 (.in(LOAD), .out(nID5));
  DiodeBackward diodebackward_3 (.in(ADD), .out(nID5));
  DiodeBackward diodebackward_4 (.in(SUB), .out(nID5));
  DiodeBackward diodebackward_5 (.in(nJMP), .out(nID5));
  PullUp pullup_2 (.out(nID5));
  DiodeBackward diodebackward_6 (.in(SUB), .out(nID4));
  PullUp pullup_3 (.out(nID4));
  PullUp pullup_4 (.out(nID3));
  DiodeBackward diodebackward_7 (.in(SUB), .out(nID3));
  PullUp pullup_5 (.out(nID2));
  DiodeBackward diodebackward_8 (.in(AND), .out(nID1));
  DiodeBackward diodebackward_9 (.in(OR), .out(nID1));
  PullUp pullup_6 (.out(nID1));
  DiodeBackward diodebackward_10 (.in(LOAD), .out(nID0));
  DiodeBackward diodebackward_11 (.in(OR), .out(nID0));
  DiodeBackward diodebackward_12 (.in(XOR), .out(nID0));
  DiodeBackward diodebackward_13 (.in(ADD), .out(nID0));
  DiodeBackward diodebackward_14 (.in(SUB), .out(nID0));
  DiodeBackward diodebackward_15 (.in(ST), .out(nID0));
  Seven_Seg_Hex seven_seg_hex_5 (.d(U6_pin6), .dp(1'b0));
  PullUp pullup_7 (.out(nID0));
  Seven_Seg_Hex seven_seg_hex_6 (.d({U6_pin10, Aout}), .dp(1'b0));
  _74164 U6 (
    .pin1(1'b1), .pin2(Fout), .pin3(U6_pin6[3]), .pin4(U6_pin6[2]), .pin5(U6_pin6[1]), .pin6(U6_pin6[0]),
    .pin7(1'b0), .pin8(GCLK), .pin9(CLR), .pin10(U6_pin10[3]), .pin11(U6_pin10[2]), .pin12(U6_pin10[1]),
    .pin13(Aout), .pin14(1'b1));
  _74540 U2 (
    .pin1(1'b0), .pin2(nID0), .pin3(nID1), .pin4(nID2), .pin5(nID3), .pin6(nID4), .pin7(nID5), .pin8(nID6),
    .pin9(nZERO), .pin10(1'b0), .pin11(Z), .pin12(CLA), .pin13(F), .pin14(C), .pin15(nB), .pin16(nA),
    .pin17(I1), .pin18(I0), .pin19(1'b0), .pin20(1'b1));
  nand nand_2 (nand_2_out, clk, clk);
  nand nand_3 (GCLK, nand_2_out, RST);
  nand nand_4 (RST, RES, nand_5_out);
  nand nand_5 (nand_5_out, RST, T0);
  xor xor_1 (xor_1_out, Aout, nA);
  xor xor_2 (xor_2_out, nB, Bout);
  nand nand_6 (nand_6_out, SETC, C);
  nand nand_7 (nand_7_out, C, C);
  nand nand_8 (CLR, LDA, CLA);
  xor xor_3 (xor_3_out, xor_1_out, xor_2_out);
  nand nand_9 (nand_9_out, nand_7_out, LDA);
  _74161 U8 (
    .pin1(RST), .pin2(clk), .pin3(1'b0), .pin4(1'b0), .pin5(1'b0), .pin6(1'b0), .pin7(1'b1), .pin8(1'b0),
    .pin9(1'b1), .pin10(1'b1), .pin11(CL3), .pin12(CL2), .pin13(CL1), .pin14(CL0), .pin15(U8_pin15),
    .pin16(1'b1));
  xor xor_4 (xor_4_out, xor_3_out, Cin);
  nand nand_10 (nand_10_out, xor_3_out, Cin);
  nand nand_11 (nand_11_out, xor_1_out, xor_2_out);
  nand nand_12 (nand_12_out, nand_10_out, nand_11_out);
  Seven_Seg_Hex seven_seg_hex_7 (.d({CL3, CL2, CL1, CL0}), .dp(1'b0));
  nand nand_13 (nand_13_out, xor_4_out, I0);
  nand nand_14 (nand_14_out, I1, nand_12_out);
  nand nand_15 (nand_15_out, nand_12_out, F);
  _7474 U9 (
    .pin1(1'b1), .pin2(U8_pin15), .pin3(clk), .pin4(1'b1), .pin5(RUN_t), .pin6(T0), .pin7(1'b0), .pin9(Cin),
    .pin10(nand_6_out), .pin11(GCLK), .pin12(Cout), .pin13(nand_9_out), .pin14(1'b1));  // open: pin8
  nand nand_16 (Fout, nand_13_out, nand_14_out);
  nand nand_17 (Cout, nand_15_out, nand_15_out);

  assign CLK_2 = clk;

  // Notes on the sheet:
  //   clk: Hz: 2147483647
  //   STEP_nRUN: default 1
  //   byter
  //   STEP/RUN
  //   16 bit Shift Register B
  //   ENTER L
  //   INSTRUCTION DECODER
  //   CLA
  //   F
  //   ~B
  //   C
  //   ~A
  //   ACCUMULATOR
  //   16 bit Shift Register A
  //   I1
  //   I0
  //   LOAD
  //   AND
  //   OR
  //   XOR
  //   ADD
  //   SUB
  //   STORE
  //   JMP
  //   U7
  //   ALU: U10,11,12,13
  //   CLR ACC
  //   Byter-01  8-Bit serial CPU Testbed
  //   Any residual carry is cleared before an operation
  //   Carry is only set before Bit 0 of an operation
  //   # Clock
  //   Clock Sequencer
  //   Suppress Carry
  //   Carry FF
endmodule
