// Digital circuit Byter_03.dig as structural Verilog
module Byter_03 (
  input  clk,
  input  IR6,
  input  IR5,
  input  IR4,
  input  in_17,
  input  in_18,
  input  in_19,
  input  nD__gt_BUS,
  input  in_21,
  input  in_22,
  input  in_23,
  output LD,
  output RES,
  output GCLK,
  output T0,
  output nRST,
  output PC_CLK,
  output nCRES,
  output nCSET,
  output I2,
  output I3,
  output nB,
  output nCLR
);

  wire ALU_CARRY, ALU_SUM, and_1_out, Aout, Bout, BUS0, BUS1, BUS2, BUS3, BUS4, BUS5, BUS6, BUS7,
       button_1_out, button_2_out, button_3_out, button_4_out, button_5_out, button_6_out, button_7_out,
       button_8_out, button_9_out, Cin, D0, D1, D2, D3, D4, D5, D6, D7, d_ff_1_nq, d_ff_2_nq, d_ff_3_nq,
       d_ff_4_nq, d_ff_5_nq, d_ff_6_nq, diodeforward_3_out, Fout, IC16_2_nq, IC16_nq, IR0, IR1, IR2, IR3,
       IR4_t, IR5_t, IR6_t, IR7, IX, LD_t, nand_5_out, nCSup, nJMP, not_1_out, not_2_out, nRESET, nY0, nY2,
       nY3, nY4, nY5, nY6, P0, P1, P2, P3, P4, P5, P6, P7, PC0, PC1, PC2, PC3, PC4, PC5, PC6, PC7, PC8, PC9,
       PC10, PC11, PC12, PC13, PC14, PC15, PC_CARRYIN, PC_CARRYOUT, PC_DATA_IN, PC_in, PCout, QD, RCO, RST,
       SETC, U2_pin9, U13_pin8, U13_pin11, U15_pin14, xor_2_out, ZERO;
  wire [2:0] U7_pin12;

  Seven_Seg_Hex seven_seg_hex_1 (.d({PC15, PC14, PC13, PC12}), .dp(1'b0));
  Seven_Seg_Hex seven_seg_hex_2 (.d({PC11, PC10, PC9, PC8}), .dp(1'b0));
  Seven_Seg_Hex seven_seg_hex_3 (.d({PC7, PC6, PC5, PC4}), .dp(1'b0));
  _74138 U9 (
    .pin1(IR4), .pin2(IR5), .pin3(IR6), .pin4(1'b0), .pin5(1'b0), .pin6(1'b1), .pin7(nJMP), .pin8(1'b0),
    .pin9(nY6), .pin10(nY5), .pin11(nY4), .pin12(nY3), .pin13(nY2), .pin14(I2), .pin15(nY0), .pin16(1'b1));
  Reset reset_1 (.out(nRESET));
  Monoflop monoflop_1 (.C(LD), .R(1'b0), .Q(SETC), .nQ(RES));
  Monoflop monoflop_2 (.C(button_1_out), .R(1'b0), .Q(LD_t), .nQ(LD));
  Button button_1 (.out(button_1_out));
  Seven_Seg_Hex seven_seg_hex_4 (.d({PC3, PC2, PC1, PC0}), .dp(1'b0));
  LED led_1 (.in(D7));
  D_FF IC16 (.D(IC16_nq), .C(button_2_out), .Q(D7), .nQ(IC16_nq));
  Seven_Seg_Hex seven_seg_hex_5 (.d({IR7, IR6_t, IR5_t, IR4_t}), .dp(1'b0));
  LED led_2 (.in(D6));
  D_FF d_ff_1 (.D(d_ff_1_nq), .C(button_3_out), .Q(D6), .nQ(d_ff_1_nq));
  Button button_2 (.out(button_2_out));
  Seven_Seg_Hex seven_seg_hex_6 (.d({IR3, IR2, IR1, IR0}), .dp(1'b0));
  xor xor_1 (nB, 1'b1, nY5);
  xor xor_2 (xor_2_out, 1'b1, nY0);
  LED led_3 (.in(D5));
  D_FF d_ff_2 (.D(d_ff_2_nq), .C(button_4_out), .Q(D5), .nQ(d_ff_2_nq));
  Button button_3 (.out(button_3_out));
  Seven_Seg_Hex seven_seg_hex_7 (.d({D7, D6, D5, D4}), .dp(1'b0));
  LED led_4 (.in(D4));
  D_FF d_ff_3 (.D(d_ff_3_nq), .C(button_5_out), .Q(D4), .nQ(d_ff_3_nq));
  Button button_4 (.out(button_4_out));
  Seven_Seg_Hex seven_seg_hex_8 (.d({D3, D2, D1, D0}), .dp(1'b0));
  nand nand_1 (nCSup, LD_t, nY5);
  nand nand_2 (nCSET, nB, SETC);
  nand nand_3 (I3, I2, nY2);
  nand nand_4 (nCLR, LD_t, xor_2_out);
  and and_1 (and_1_out, I2, nY2, nY3);
  LED led_5 (.in(D3));
  D_FF d_ff_4 (.D(d_ff_4_nq), .C(button_6_out), .Q(D3), .nQ(d_ff_4_nq));
  Button button_5 (.out(button_5_out));
  LED led_6 (.in(D2));
  D_FF d_ff_5 (.D(d_ff_5_nq), .C(button_7_out), .Q(D2), .nQ(d_ff_5_nq));
  Button button_6 (.out(button_6_out));
  and and_2 (nCRES, 1'b1, and_1_out, nCSup);
  LED led_7 (.in(D1));
  D_FF d_ff_6 (.D(d_ff_6_nq), .C(button_8_out), .Q(D1), .nQ(d_ff_6_nq));
  Button button_7 (.out(button_7_out));
  Seven_Seg_Hex seven_seg_hex_9 (.d({BUS7, BUS6, BUS5, BUS4}), .dp(1'b0));
  LED led_8 (.in(D0));
  D_FF IC16_2 (.D(IC16_2_nq), .C(button_9_out), .Q(D0), .nQ(IC16_2_nq));
  Button button_8 (.out(button_8_out));
  Seven_Seg_Hex seven_seg_hex_10 (.d({BUS3, BUS2, BUS1, BUS0}), .dp(1'b0));
  Seven_Seg_Hex seven_seg_hex_11 (.d({D7, D6, D5, D4}), .dp(1'b0));
  Button button_9 (.out(button_9_out));
  Seven_Seg_Hex seven_seg_hex_12 (.d({D3, D2, D1, D0}), .dp(1'b0));
  nand nand_5 (nand_5_out, clk, clk);
  nand nand_6 (RST, RES, nRST);
  nand nand_7 (nRST, RST, T0);
  _74165 U5 (
    .pin1(LD), .pin2(GCLK), .pin3(D3), .pin4(D2), .pin5(D1), .pin6(D0), .pin8(1'b0), .pin9(Bout),
    .pin10(1'b0), .pin11(D7), .pin12(D6), .pin13(D5), .pin14(D4), .pin15(1'b0), .pin16(1'b1));  // open: pin7
  nand nand_8 (PC_CLK, nand_5_out, RST);
  not not_1 (not_1_out, nJMP);
  _74126 U13 (
    .pin1(nJMP), .pin2(PC_DATA_IN), .pin3(PC_in), .pin4(not_1_out), .pin5(Bout), .pin6(PC_in), .pin7(1'b0),
    .pin8(U13_pin8), .pin9(ALU_CARRY), .pin10(I3), .pin11(U13_pin11), .pin12(ALU_SUM), .pin13(I2),
    .pin14(1'b1));
  _74283 U15 (
    .pin1(PC_CARRYOUT), .pin2(1'b0), .pin3(1'b0), .pin4(PC_DATA_IN), .pin5(1'b0), .pin6(PCout),
    .pin7(PC_CARRYIN), .pin8(1'b0), .pin9(ALU_CARRY), .pin10(ALU_SUM), .pin11(Cin), .pin12(Aout),
    .pin14(U15_pin14), .pin15(1'b1), .pin16(1'b1));  // open: pin13
  not not_2 (not_2_out, QD);
  and and_3 (GCLK, 1'b1, not_2_out, PC_CLK);
  DiodeForward diodeforward_1 (.in(U13_pin11), .out(Fout));
  DiodeForward diodeforward_2 (.in(U13_pin8), .out(Fout));
  _74161 U7 (
    .pin1(RST), .pin2(clk), .pin3(1'b0), .pin4(1'b0), .pin5(1'b0), .pin6(1'b0), .pin7(1'b1), .pin8(1'b0),
    .pin9(1'b1), .pin10(1'b1), .pin11(QD), .pin12(U7_pin12[2]), .pin13(U7_pin12[1]), .pin14(U7_pin12[0]),
    .pin15(RCO), .pin16(1'b1));
  _74299 U6 (
    .pin1(in_18), .pin2(in_19), .pin3(in_19), .pin4(BUS6), .pin5(BUS4), .pin6(BUS2), .pin7(BUS0),
    .pin8(Aout), .pin9(nCLR), .pin10(1'b0), .pin11(1'b0), .pin12(GCLK), .pin13(BUS1), .pin14(BUS3),
    .pin15(BUS5), .pin16(BUS7), .pin18(Fout), .pin19(in_17), .pin20(1'b1));  // open: pin17
  PullDown pulldown_1 (.out(Fout));
  xor xor_3 (U15_pin14, Bout, nB);
  _7474 U14 (
    .pin1(nCRES), .pin2(ALU_CARRY), .pin3(GCLK), .pin4(nCSET), .pin5(Cin), .pin7(1'b0), .pin9(PC_CARRYIN),
    .pin10(LD), .pin11(GCLK), .pin12(PC_CARRYOUT), .pin13(1'b1), .pin14(1'b1));  // open: pin6, pin8
  _7474 U16 (
    .pin1(1'b1), .pin2(1'b1), .pin3(1'b1), .pin4(1'b1), .pin7(1'b0), .pin8(T0), .pin9(IX), .pin10(1'b1),
    .pin11(clk), .pin12(RCO), .pin13(1'b1), .pin14(1'b1));  // open: pin5, pin6
  Seven_Seg_Hex seven_seg_hex_13 (.d({QD, U7_pin12}), .dp(1'b0));
  // _27C1024 U1: pin names not known; wires that end beside it: 1'b1, 1'b0, IR7, IR6_t, IR5_t, IR4_t, IR3, IR2, IR1, IR0, 1'b0, P7, P6, P5, 1'b1, PC15, PC14, PC13, PC12, PC11, PC10, PC9
  // _62256 U4: pin names not known; wires that end beside it: P4, P3, P2, P1, P0, 1'b0, IR6_t, IR4_t, P7, P6, P5, P4, P3, P2, P1, P0, BUS0, BUS1, BUS2, 1'b0, PC1, PC0, 1'b1, in_21, IR5_t, IR0, IR1, IR3, in_22, IR2, in_23, BUS7
  _74595 U2 (
    .pin1(PC14), .pin2(PC13), .pin3(PC12), .pin4(PC11), .pin5(PC10), .pin6(PC9), .pin7(PC8), .pin8(1'b0),
    .pin9(U2_pin9), .pin10(nRESET), .pin11(PC_CLK), .pin12(nRST), .pin13(1'b0), .pin14(PC_in), .pin15(PC15),
    .pin16(1'b1));
  _74595 U3 (
    .pin1(PC6), .pin2(PC5), .pin3(PC4), .pin4(PC3), .pin5(PC2), .pin6(PC1), .pin7(PC0), .pin8(1'b0),
    .pin9(PCout), .pin10(nRESET), .pin11(PC_CLK), .pin12(nRST), .pin13(1'b0), .pin14(U2_pin9), .pin15(PC7),
    .pin16(1'b1));
  DiodeForward diodeforward_3 (.in(BUS7), .out(diodeforward_3_out));
  DiodeForward diodeforward_4 (.in(BUS6), .out(diodeforward_3_out));
  DiodeForward diodeforward_5 (.in(BUS5), .out(diodeforward_3_out));
  DiodeForward diodeforward_6 (.in(BUS4), .out(diodeforward_3_out));
  DiodeForward diodeforward_7 (.in(BUS3), .out(diodeforward_3_out));
  DiodeForward diodeforward_8 (.in(BUS2), .out(diodeforward_3_out));
  DiodeForward diodeforward_9 (.in(BUS1), .out(diodeforward_3_out));
  DiodeForward diodeforward_10 (.in(BUS0), .out(diodeforward_3_out));
  PullDown pulldown_2 (.out(diodeforward_3_out));
  xor xor_4 (ZERO, 1'b1, diodeforward_3_out);
  LED led_9 (.in(ZERO));

  // Other names for the same wires on the sheet: D_BUS = nD__gt_BUS; I1 = I3; I4 = IR4; I5 = IR5; I6 = IR6;
  //   M0 = in_18; M1 = in_17; nLOAD = LD; nOERAM = in_22; nRAMCE = in_23; nRES = RES; nWE = in_19; nWERAM = in_21;
  //   I0 = I2; nY1 = I2; nY7 = nJMP; RCLK = nRST

  // Notes on the sheet:
  //   clk: Hz: 2147483647
  //   in_17: default 1
  //   nD__gt_BUS: default 1
  //   in_21: default 1
  //   in_22: default 1
  //   in_23: default 1
  //   BYTER 03
  //   INSTRUCTION DECODER
  //   DATA INPUT
  //   BYTER 8-bit  Bit serial CPU Testbed
  //   PC ADDRESS
  //   STEP/RUN
  //   U12B
  //   INSTR.      DATA
  //   U12C
  //   Suppress Carry
  //   74HC00
  //   74HC11
  //   U11A
  //   U10
  //   U11B
  //   AC / BUS
  //   CLOCK SEQUENCER
  //   REGISTERS
  //   ALU
  //   U8
  //   B-REGISTER
  //   PC / ALU MUX
  //   U11C
  //   ACCUMULATOR
  //   U12D
  //   Carry FF
  //   # Clock
  //   PC Carry FF
  //   PROGRAM COUNTER ROM & RAM
  //   U12A
  //   ZERO
endmodule
